// Logisim project cpu2.circ as structural Verilog: 9 circuits, main circuit 1 bit Alu
module _1_bit_Alu (
  input  Binvert,
  input  Ainvert,
  input  [1:0] operation,
  input  cin,
  input  a,
  input  b,
  input  Less,
  output Result,
  output out_9
);

  wire adder_1_out, and_1_out, multiplexer_1_out, multiplexer_2_out, not_1_out, not_2_out, or_1_out;

  not not_1 (not_1_out, b);
  Multiplexer #(.enable("false")) multiplexer_1 (.in0(a), .in1(not_2_out), .out(multiplexer_1_out), .sel(Ainvert));
  not not_2 (not_2_out, a);
  Multiplexer #(.enable("false")) multiplexer_2 (.in0(b), .in1(not_1_out), .out(multiplexer_2_out), .sel(Binvert));
  and and_1 (and_1_out, multiplexer_1_out, multiplexer_2_out);
  or or_1 (or_1_out, multiplexer_1_out, multiplexer_2_out);
  Adder #(.width(1)) adder_1 (.a(multiplexer_1_out), .b(multiplexer_2_out), .out(adder_1_out), .cin(cin), .cout(out_9));
  Multiplexer #(.select(2), .enable("false")) multiplexer_3 (
    .in0(and_1_out), .in1(or_1_out), .in2(adder_1_out), .in3(Less), .out(Result), .sel(operation));
endmodule

module Alu (
  input  Ainv,
  input  Bnegate,
  input  [1:0] op,
  input  [15:0] B,
  input  [15:0] A,
  output [15:0] Result,
  output zero,
  output overflow,
  output cout
);

  wire alu_1_bit_2_1_set, n1_bit_alu_1_out_9, n1_bit_alu_2_out_9, n1_bit_alu_3_out_9, n1_bit_alu_4_out_9,
       n1_bit_alu_5_out_9, n1_bit_alu_6_out_9, n1_bit_alu_7_out_9, n1_bit_alu_8_out_9, n1_bit_alu_9_out_9,
       n1_bit_alu_10_out_9, n1_bit_alu_11_out_9, n1_bit_alu_12_out_9, n1_bit_alu_13_out_9,
       n1_bit_alu_14_out_9, n1_bit_alu_15_out_9, not_1_out;

  _1_bit_Alu u_1_bit_alu_1 (
    .a(A[0]), .b(B[0]), .Less(alu_1_bit_2_1_set), .Result(Result[0]), .Binvert(Bnegate), .Ainvert(Ainv),
    .cin(Bnegate), .out_9(n1_bit_alu_1_out_9), .operation(op));
  _1_bit_Alu u_1_bit_alu_2 (
    .a(A[1]), .b(B[1]), .Less(1'b0), .Result(Result[1]), .Binvert(Bnegate), .Ainvert(Ainv),
    .cin(n1_bit_alu_1_out_9), .out_9(n1_bit_alu_2_out_9), .operation(op));
  _1_bit_Alu u_1_bit_alu_3 (
    .a(A[2]), .b(B[2]), .Less(1'b0), .Result(Result[2]), .Binvert(Bnegate), .Ainvert(Ainv),
    .cin(n1_bit_alu_2_out_9), .out_9(n1_bit_alu_3_out_9), .operation(op));
  _1_bit_Alu u_1_bit_alu_4 (
    .a(A[3]), .b(B[3]), .Less(1'b0), .Result(Result[3]), .Binvert(Bnegate), .Ainvert(Ainv),
    .cin(n1_bit_alu_3_out_9), .out_9(n1_bit_alu_4_out_9), .operation(op));
  _1_bit_Alu u_1_bit_alu_5 (
    .a(A[4]), .b(B[4]), .Less(1'b0), .Result(Result[4]), .Binvert(Bnegate), .Ainvert(Ainv),
    .cin(n1_bit_alu_4_out_9), .out_9(n1_bit_alu_5_out_9), .operation(op));
  _1_bit_Alu u_1_bit_alu_6 (
    .a(A[5]), .b(B[5]), .Less(1'b0), .Result(Result[5]), .Binvert(Bnegate), .Ainvert(Ainv),
    .cin(n1_bit_alu_5_out_9), .out_9(n1_bit_alu_6_out_9), .operation(op));
  _1_bit_Alu u_1_bit_alu_7 (
    .a(A[6]), .b(B[6]), .Less(1'b0), .Result(Result[6]), .Binvert(Bnegate), .Ainvert(Ainv),
    .cin(n1_bit_alu_6_out_9), .out_9(n1_bit_alu_7_out_9), .operation(op));
  _1_bit_Alu u_1_bit_alu_8 (
    .a(A[7]), .b(B[7]), .Less(1'b0), .Result(Result[7]), .Binvert(Bnegate), .Ainvert(Ainv),
    .cin(n1_bit_alu_7_out_9), .out_9(n1_bit_alu_8_out_9), .operation(op));
  _1_bit_Alu u_1_bit_alu_9 (
    .a(A[8]), .b(B[8]), .Less(1'b0), .Result(Result[8]), .Binvert(Bnegate), .Ainvert(Ainv),
    .cin(n1_bit_alu_8_out_9), .out_9(n1_bit_alu_9_out_9), .operation(op));
  _1_bit_Alu u_1_bit_alu_10 (
    .a(A[9]), .b(B[9]), .Less(1'b0), .Result(Result[9]), .Binvert(Bnegate), .Ainvert(Ainv),
    .cin(n1_bit_alu_9_out_9), .out_9(n1_bit_alu_10_out_9), .operation(op));
  _1_bit_Alu u_1_bit_alu_11 (
    .a(A[10]), .b(B[10]), .Less(1'b0), .Result(Result[10]), .Binvert(Bnegate), .Ainvert(Ainv),
    .cin(n1_bit_alu_10_out_9), .out_9(n1_bit_alu_11_out_9), .operation(op));
  _1_bit_Alu u_1_bit_alu_12 (
    .a(A[11]), .b(B[11]), .Less(1'b0), .Result(Result[11]), .Binvert(Bnegate), .Ainvert(Ainv),
    .cin(n1_bit_alu_11_out_9), .out_9(n1_bit_alu_12_out_9), .operation(op));
  _1_bit_Alu u_1_bit_alu_13 (
    .a(A[12]), .b(B[12]), .Less(1'b0), .Result(Result[12]), .Binvert(Bnegate), .Ainvert(Ainv),
    .cin(n1_bit_alu_12_out_9), .out_9(n1_bit_alu_13_out_9), .operation(op));
  _1_bit_Alu u_1_bit_alu_14 (
    .a(A[13]), .b(B[13]), .Less(1'b0), .Result(Result[13]), .Binvert(Bnegate), .Ainvert(Ainv),
    .cin(n1_bit_alu_13_out_9), .out_9(n1_bit_alu_14_out_9), .operation(op));
  _1_bit_Alu u_1_bit_alu_15 (
    .a(A[14]), .b(B[14]), .Less(1'b0), .Result(Result[14]), .Binvert(Bnegate), .Ainvert(Ainv),
    .cin(n1_bit_alu_14_out_9), .out_9(n1_bit_alu_15_out_9), .operation(op));
  ALU_1_bit_2 alu_1_bit_2_1 (
    .a(A[15]), .b(B[15]), .Less(1'b0), .Result(Result[15]), .Set(alu_1_bit_2_1_set), .cout(cout),
    .overflow(overflow), .Binvert(Bnegate), .Ainvert(Ainv), .cin(n1_bit_alu_15_out_9), .operation(op));
  nor nor_1 (zero, Result[15], Result[14], Result[13], Result[12], Result[11], Result[10], Result[9], Result[8], Result[7], Result[6], Result[5], Result[4], Result[3], Result[2], Result[1], Result[0]);
  not not_1 (not_1_out, overflow);
  // AND_Gate and_1 has open pins: in1=not_1_out, out=open
endmodule

module register_file (
  input  [2:0] read_register_1,
  input  [2:0] read_register_2,
  input  regWrite,
  input  [2:0] write_register,
  input  [15:0] write_data,
  input  clock,
  output [15:0] read_data2,
  output [15:0] read_data2_2
);

  wire and_1_out, and_2_out, and_3_out, and_4_out, and_5_out, and_6_out, and_7_out, and_8_out,
       decoder_1_out0, decoder_1_out1, decoder_1_out2, decoder_1_out3, decoder_1_out4, decoder_1_out5,
       decoder_1_out6, decoder_1_out7;
  wire [15:0] _0_q, _1_q, _2_q, _3_q, _4_q, _5_q, _6_q, _7_q;

  Decoder #(.select(3), .enable("false")) decoder_1 (
    .out0(decoder_1_out0), .out1(decoder_1_out1), .out2(decoder_1_out2), .out3(decoder_1_out3),
    .out4(decoder_1_out4), .out5(decoder_1_out5), .out6(decoder_1_out6), .out7(decoder_1_out7),
    .sel(write_register));
  and and_1 (and_1_out, decoder_1_out0, regWrite);
  and and_2 (and_2_out, decoder_1_out1, regWrite);
  and and_3 (and_3_out, decoder_1_out2, regWrite);
  and and_4 (and_4_out, decoder_1_out3, regWrite);
  and and_5 (and_5_out, decoder_1_out4, regWrite);
  and and_6 (and_6_out, decoder_1_out5, regWrite);
  and and_7 (and_7_out, decoder_1_out6, regWrite);
  and and_8 (and_8_out, decoder_1_out7, regWrite);
  Register #(.width(16)) _0 (.D({16{1'b0}}), .en(and_1_out), .Q(_0_q), .clk(clock), .clr(1'b0));
  Register #(.width(16)) _1 (.D(write_data), .en(and_2_out), .Q(_1_q), .clk(clock), .clr(1'b0));
  Register #(.width(16)) _2 (.D(write_data), .en(and_3_out), .Q(_2_q), .clk(clock), .clr(1'b0));
  Register #(.width(16)) _3 (.D(write_data), .en(and_4_out), .Q(_3_q), .clk(clock), .clr(1'b0));
  Register #(.width(16)) _4 (.D(write_data), .en(and_5_out), .Q(_4_q), .clk(clock), .clr(1'b0));
  Register #(.width(16)) _5 (.D(write_data), .en(and_6_out), .Q(_5_q), .clk(clock), .clr(1'b0));
  Register #(.width(16)) _6 (.D(write_data), .en(and_7_out), .Q(_6_q), .clk(clock), .clr(1'b0));
  Register #(.width(16)) _7 (.D(write_data), .en(and_8_out), .Q(_7_q), .clk(clock), .clr(1'b0));
  Multiplexer #(.select(3), .width(16), .enable("false")) multiplexer_1 (
    .in0(_0_q), .in1(_1_q), .in2(_2_q), .in3(_3_q), .in4(_4_q), .in5(_5_q), .in6(_6_q), .in7(_7_q),
    .out(read_data2), .sel(read_register_1));
  Multiplexer #(.select(3), .width(16), .enable("false")) multiplexer_2 (
    .in0(_0_q), .in1(_1_q), .in2(_2_q), .in3(_3_q), .in4(_4_q), .in5(_5_q), .in6(_6_q), .in7(_7_q),
    .out(read_data2_2), .sel(read_register_2));
endmodule

module main (
);

  wire alu_1_zero, alu_control_1_ainv, alu_control_1_bnegate, and_1_out, Clear_PC_out, clock_1_out,
       control_1_alu_op1, control_1_alu_op2, control_1_alusrc, control_1_branch, control_1_jalr,
       control_1_lui, control_1_memread, control_1_memtoreg, control_1_memwrite, control_1_regrt,
       control_1_regwrite, multiplexer_5_out, not_1_out, not_2_out, Read_Array_out, Zero_Counter_out;
  wire [1:0] alu_control_1_op2;
  wire [2:0] multiplexer_1_out;
  wire [15:0] adder_1_out, adder_2_out, alu_1_result, counter_1_q, multiplexer_2_out, multiplexer_3_out,
       multiplexer_4_out, multiplexer_6_out, multiplexer_7_out, multiplexer_8_out, multiplexer_9_out,
       multiplexer_10_out, PC_q, ram_1_data, ram_2_data, register_file_1_read_data2,
       register_file_1_read_data2_2, rom_1_data, rom_2_data, shift_lui_1_out_2, sign_extention_1_out_2;

  Register #(.width(16)) PC (.D(multiplexer_7_out), .Q(PC_q), .clk(clock_1_out), .clr(Clear_PC_out));  // open: en
  not not_1 (not_1_out, 1'b0);
  Button Clear_PC (.out(Clear_PC_out));
  Adder #(.width(16)) adder_1 (.a(16'h1), .b(PC_q), .out(adder_1_out), .cin(1'b0));  // open: cout
  RAM #(.addrWidth(16), .dataWidth(16), .bus("separate")) ram_1 (
    .addr(PC_q), .din(rom_1_data), .data(ram_1_data), .str(not_1_out), .sel(not_1_out), .clk(clock_1_out),
    .ld(not_1_out), .clr(1'b0));
  ROM #(.addrWidth(16), .dataWidth(16)) rom_1 (.addr(PC_q), .data(rom_1_data), .sel(not_1_out));
  CONTROL control_1 (
    .in_1(ram_1_data[15:13]), .ALUSrc(control_1_alusrc), .RegRt(control_1_regrt),
    .RegWrite(control_1_regwrite), .MemWrite(control_1_memwrite), .MemRead(control_1_memread),
    .MemToReg(control_1_memtoreg), .Branch(control_1_branch), .jalr(control_1_jalr), .lui(control_1_lui),
    .ALU_OP1(control_1_alu_op1), .ALU_OP2(control_1_alu_op2));
  Sign_Extention sign_extention_1 (.in_1(ram_1_data[6:0]), .out_2(sign_extention_1_out_2));
  Multiplexer #(.width(3), .enable("false")) multiplexer_1 (
    .in0(ram_1_data[12:10]), .in1(ram_1_data[2:0]), .out(multiplexer_1_out), .sel(control_1_regrt));
  Shift_Lui shift_lui_1 (.Ten(ram_1_data[9:0]), .out_2(shift_lui_1_out_2));
  Clock clock_1 (.out(clock_1_out));
  register_file register_file_1 (
    .read_register_1(ram_1_data[9:7]), .read_register_2(multiplexer_1_out), .regWrite(control_1_regwrite),
    .write_register(ram_1_data[12:10]), .write_data(multiplexer_10_out), .clock(clock_1_out),
    .read_data2(register_file_1_read_data2), .read_data2_2(register_file_1_read_data2_2));
  Multiplexer #(.width(16), .enable("false")) multiplexer_2 (
    .in0(register_file_1_read_data2_2), .in1(sign_extention_1_out_2), .out(multiplexer_2_out),
    .sel(control_1_alusrc));
  ALU_CONTROL alu_control_1 (
    .ALU_OP1(control_1_alu_op1), .ALU_OP2(control_1_alu_op2), .Bnegate(alu_control_1_bnegate),
    .Ainv(alu_control_1_ainv), .OP1(alu_control_1_op2[1]), .OP2(alu_control_1_op2[0]));
  Adder #(.width(16)) adder_2 (
    .a(adder_1_out), .b(sign_extention_1_out_2), .out(adder_2_out), .cin(1'b0));  // open: cout
  Alu alu_1 (
    .A(register_file_1_read_data2), .op(alu_control_1_op2), .B(multiplexer_2_out), .Result(alu_1_result),
    .Ainv(alu_control_1_ainv), .Bnegate(alu_control_1_bnegate), .zero(alu_1_zero));  // open: overflow, cout
  Multiplexer #(.width(16), .enable("false")) multiplexer_3 (
    .in0(alu_1_result), .in1(counter_1_q), .out(multiplexer_3_out), .sel(Read_Array_out));
  and and_1 (and_1_out, control_1_branch, alu_1_zero);
  Multiplexer #(.width(16), .enable("false")) multiplexer_4 (
    .in0(register_file_1_read_data2_2), .in1(rom_2_data), .out(multiplexer_4_out), .sel(Read_Array_out));
  Multiplexer #(.enable("false")) multiplexer_5 (
    .in0(control_1_memwrite), .in1(not_2_out), .out(multiplexer_5_out), .sel(Read_Array_out));
  Multiplexer #(.width(16), .enable("false")) multiplexer_6 (
    .in0(adder_1_out), .in1(adder_2_out), .out(multiplexer_6_out), .sel(and_1_out));
  RAM #(.addrWidth(16), .dataWidth(16), .bus("separate")) ram_2 (
    .addr(multiplexer_3_out), .din(multiplexer_4_out), .data(ram_2_data), .str(multiplexer_5_out),
    .sel(not_2_out), .clk(clock_1_out), .ld(control_1_memread), .clr(1'b0));
  not not_2 (not_2_out, 1'b0);
  Multiplexer #(.width(16), .enable("false")) multiplexer_7 (
    .in0(multiplexer_6_out), .in1(register_file_1_read_data2), .out(multiplexer_7_out), .sel(control_1_jalr));
  Multiplexer #(.width(16), .enable("false")) multiplexer_8 (
    .in0(alu_1_result), .in1(ram_2_data), .out(multiplexer_8_out), .sel(control_1_memtoreg));
  Button Read_Array (.out(Read_Array_out));
  Counter #(.width(16), .max('hffff)) counter_1 (
    .Q(counter_1_q), .clk(clock_1_out), .clr(Zero_Counter_out));  // open: load, D, count, carry
  ROM #(.addrWidth(16), .dataWidth(16)) rom_2 (.addr(counter_1_q), .data(rom_2_data), .sel(not_2_out));
  Multiplexer #(.width(16), .enable("false")) multiplexer_9 (
    .in0(multiplexer_8_out), .in1(adder_1_out), .out(multiplexer_9_out), .sel(control_1_jalr));
  Button Zero_Counter (.out(Zero_Counter_out));
  Multiplexer #(.width(16), .enable("false")) multiplexer_10 (
    .in0(multiplexer_9_out), .in1(shift_lui_1_out_2), .out(multiplexer_10_out), .sel(control_1_lui));

  // Notes on the sheet:
  //   contents of rom_1 (hex, n*v repeats v):
  //   c00 400 3003 a880 c803 d82 2481 e200 8481 8c82 bc81 b882 934*0 cc
  //   contents of rom_2 (hex, n*v repeats v):
  //   1 2 3 4 5 6 7 8 9
endmodule

module ALU_1_bit_2 (
  input  Binvert,
  input  Ainvert,
  input  [1:0] operation,
  input  cin,
  input  a,
  input  b,
  input  Less,
  output Result,
  output Set,
  output cout,
  output overflow
);

  wire and_1_out, multiplexer_1_out, multiplexer_2_out, not_1_out, not_2_out, or_1_out;

  not not_1 (not_1_out, b);
  Multiplexer #(.enable("false")) multiplexer_1 (.in0(a), .in1(not_2_out), .out(multiplexer_1_out), .sel(Ainvert));
  not not_2 (not_2_out, a);
  Multiplexer #(.enable("false")) multiplexer_2 (.in0(b), .in1(not_1_out), .out(multiplexer_2_out), .sel(Binvert));
  and and_1 (and_1_out, multiplexer_1_out, multiplexer_2_out);
  or or_1 (or_1_out, multiplexer_1_out, multiplexer_2_out);
  Adder #(.width(1)) adder_1 (.a(multiplexer_1_out), .b(multiplexer_2_out), .out(Set), .cin(cin), .cout(cout));
  Multiplexer #(.select(2), .enable("false")) multiplexer_3 (
    .in0(and_1_out), .in1(or_1_out), .in2(Set), .in3(Less), .out(Result), .sel(operation));
  xor xor_1 (overflow, cin, cout);
endmodule

module Sign_Extention (
  input  [6:0] in_1,
  output [15:0] out_2
);


  assign out_2 = {{10{in_1[6]}}, in_1[5:0]};
endmodule

module Shift_Lui (
  input  [9:0] Ten,
  output [15:0] out_2
);


  assign out_2 = {Ten, {6{1'b0}}};
endmodule

module ALU_CONTROL (
  input  ALU_OP1,
  input  ALU_OP2,
  output Ainv,
  output Bnegate,
  output OP1,
  output OP2
);

  not not_1 (Bnegate, ALU_OP1);
  not not_2 (OP1, 1'b0);

  assign Ainv = 1'b0;
  assign OP2 = ALU_OP2;
endmodule

module CONTROL (
  input  [2:0] in_1,
  output ALUSrc,
  output RegRt,
  output RegWrite,
  output MemWrite,
  output MemRead,
  output MemToReg,
  output Branch,
  output jalr,
  output lui,
  output ALU_OP1,
  output ALU_OP2
);

  wire and_1_out, not_1_out, not_2_out, not_3_out, not_4_out, not_5_out, not_7_out, or_2_out, or_3_out,
       xor_1_out;

  not not_1 (not_1_out, in_1[1]);
  not not_2 (not_2_out, in_1[2]);
  and and_1 (and_1_out, in_1[2], not_1_out);
  not not_3 (not_3_out, in_1[0]);
  or or_1 (ALUSrc, and_1_out, in_1[0]);
  or or_2 (or_2_out, in_1[2], in_1[0]);
  or or_3 (or_3_out, not_2_out, in_1[1], in_1[0]);
  and and_2 (MemRead, in_1[2], not_4_out, in_1[0]);
  not not_4 (not_4_out, in_1[1]);
  and and_3 (Branch, in_1[2], in_1[1], not_3_out);
  and and_4 (jalr, in_1[2], in_1[1], in_1[0]);
  not not_5 (not_5_out, in_1[1]);
  not not_6 (RegRt, or_2_out);
  not not_7 (not_7_out, in_1[0]);
  not not_8 (MemWrite, or_3_out);
  and and_5 (lui, not_2_out, in_1[1], in_1[0]);
  xor xor_1 (xor_1_out, in_1[1], in_1[0]);
  nor nor_1 (ALU_OP2, in_1[2], not_5_out, in_1[0]);
  nand nand_1 (ALU_OP1, in_1[1], xor_1_out);
  nand nand_2 (RegWrite, in_1[2], not_7_out);

  assign MemToReg = MemRead;
endmodule
